# Fritzing sketch Noise (saved by Fritzing 0.7.10b)
breadboards: 1

parts:
  Arduino1 = Arduino
  LED1 = LED - 5mm [color="Red (633nm)" package="5 mm [THT]"]
  R1 = Resistor [tolerance=±5% resistance=220 package=THT]
  SPKR1 = Loudspeaker

nets:
  N1: Arduino1.D9, R1.Pin_1
  N2: Arduino1.D3, SPKR1.pin2
  N3: Arduino1.GND, LED1.cathode, SPKR1.pin1
  N4: LED1.anode, R1.Pin_0
