# Fritzing sketch Sound_Light (saved by Fritzing 0.7.10b)
breadboards: 1

parts:
  Arduino1 = Arduino
  LED1 = LED - 5mm [color="Red (633nm)" package="5 mm [THT]"]
  R1 = Resistor [tolerance=±5% resistance=220 package=THT]
  SPKR1 = Loudspeaker
  R2 = Rotary Potentiometer (Large) [maximum_resistance=100kΩ package=THT]

nets:
  N1: Arduino1.D9, R1.Pin_1
  N2: Arduino1.D3, SPKR1.pin2
  N3: Arduino1.+5V, R2.leg2
  N4: Arduino1.GND, LED1.cathode, SPKR1.pin1, R2.leg1
  N5: Arduino1.A0, R2.wiper
  N6: LED1.anode, R1.Pin_0
