# Fritzing sketch Sequencer-4pots (saved by Fritzing 0.7.10b)
breadboards: 1

parts:
  part = Arduino
  SPEAKER = Loudspeaker  # not connected
  POT_1 = Rotary Potentiometer (Large) [package=THT]
  POT_2 = Rotary Potentiometer (Large) [package=THT]
  POT_3 = Rotary Potentiometer (Large) [package=THT]
  POT_4 = Rotary Potentiometer (Large) [package=THT]
  LED1 = Red LED - 5mm
  LED1_2 = Red LED - 5mm
  LED1_3 = Red LED - 5mm
  LED1_4 = Red LED - 5mm
  R_220 = Resistor [resistance=220 tolerance=±5% package=THT]
  R_220_2 = Resistor [resistance=220 tolerance=±5% package=THT]
  R_220_3 = Resistor [resistance=220 tolerance=±5% package=THT]
  R_220_4 = Resistor [resistance=220 tolerance=±5% package=THT]
  R1 = Rotary Potentiometer (Large) [maximum_resistance=100kΩ package=THT]  # not connected

nets (from the schematic view):
  N1: part.GND, R_220.Pin_1, R_220_2.Pin_1, R_220_3.Pin_1, R_220_4.Pin_1
  N2: part.D5, LED1_4.anode
  N3: part.D4, LED1_3.anode
  N4: part.D3, LED1_2.anode
  N5: part.D2, LED1.anode
  N6: part.+5V, POT_1.leg1, POT_2.leg1, POT_3.leg1, POT_4.leg1
  N7: part.A0, POT_1.wiper
  N8: part.A1, POT_2.wiper
  N9: part.A2, POT_3.wiper
  N10: part.A3, POT_4.wiper
  N11: POT_1.leg2, POT_2.leg2, POT_3.leg2, POT_4.leg2
  N12: LED1.cathode, R_220.Pin_0
  N13: LED1_2.cathode, R_220_2.Pin_0
  N14: LED1_3.cathode, R_220_3.Pin_0
  N15: LED1_4.cathode, R_220_4.Pin_0
