# Fritzing sketch Blink (saved by Fritzing 0.7.12b)

parts:
  Arduino_LiliyPad1 = Arduino LilyPad
  R1 = Resistor [tolerance=±5% resistance=220 package=THT]
  LED1 = LED - 5mm [color="Red (633nm)" package="5 mm [THT]"]

nets:
  N1: Arduino_LiliyPad1.D4, LED1.anode
  N2: Arduino_LiliyPad1.POW, R1.Pin_1
  N3: R1.Pin_0, LED1.cathode

notes:
  In this very simple example, LilyPad Arduino will be programmed to blink the LED on pin 5. Related example: http://arduino.cc/en/Tutorial/Blink

// code stored in the sketch: Blink.ino
/*
  Blink
  Turns on an LED on for one second, then off for one second, repeatedly.
 
  This example code is in the public domain.
 */

void setup() {                
  // initialize the digital pin as an output.
  // Pin 13 has an LED connected on most Arduino boards:
  pinMode(13, OUTPUT);     
}

void loop() {
  digitalWrite(13, HIGH);   // set the LED on
  delay(1000);              // wait for a second
  digitalWrite(13, LOW);    // set the LED off
  delay(1000);              // wait for a second
}
