# Fritzing sketch Noise (saved by Fritzing 0.7.12b)
breadboards: 1

parts:
  LED1 = LED - 5mm [color="Red (633nm)" package="5 mm [THT]"]
  R1 = Resistor [tolerance=±5% resistance=220 package=THT]
  SPKR1 = Loudspeaker
  Arduino_LiliyPad1 = Arduino LilyPad

nets:
  N1: LED1.cathode, SPKR1.pin1, Arduino_LiliyPad1.GND
  N2: LED1.anode, R1.Pin_0
  N3: R1.Pin_1, Arduino_LiliyPad1.D4
  N4: SPKR1.pin2, Arduino_LiliyPad1.D3
