# Fritzing sketch Sound_Light (saved by Fritzing 0.7.12b)
breadboards: 1

parts:
  LED1 = LED - 5mm [color="Red (633nm)" package="5 mm [THT]"]
  R1 = Resistor [tolerance=±5% resistance=220 package=THT]
  SPKR1 = Loudspeaker
  R2 = Rotary Potentiometer (Large) [maximum_resistance=100kΩ package=THT]
  Arduino_LiliyPad1 = Arduino LilyPad

nets:
  N1: LED1.cathode, SPKR1.pin1, R2.leg1, Arduino_LiliyPad1.GND
  N2: LED1.anode, R1.Pin_0
  N3: R1.Pin_1, Arduino_LiliyPad1.D4
  N4: SPKR1.pin2, Arduino_LiliyPad1.D3
  N5: R2.wiper, Arduino_LiliyPad1.A0
  N6: R2.leg2, Arduino_LiliyPad1.POW
