# Fritzing sketch PushbuttonRead (saved by Fritzing 0.7.12b)
breadboards: 1

parts:
  LED1 = LED - 5mm [color="Red (633nm)" package="5 mm [THT]"]
  R1 = Resistor [tolerance=±5% resistance=220 package=THT]
  Arduino_LiliyPad1 = Arduino LilyPad
  RE1 = Rotary Encoder [package=THT]
  R2 = Resistor [tolerance=±5% resistance=220 package=THT]

nets:
  N1: LED1.cathode, Arduino_LiliyPad1.GND
  N2: LED1.anode, R1.Pin_0
  N3: R1.Pin_1, Arduino_LiliyPad1.D4
  N4: Arduino_LiliyPad1.D12, RE1.EncoderPinB, R2.Pin_0
  N5: Arduino_LiliyPad1.POW, R2.Pin_1
